// Logisim project 4BitCounter.circ as structural Verilog
module main (
  input  in_1,
  input  [3:0] in_2,
  input  in_3,
  output out_4,
  output out_5,
  output out_6,
  output out_7,
  output out_8,
  output out_9,
  output out_10,
  output out_11
);

  wire and_1_out, and_2_out, and_3_out, and_4_out, and_5_out, and_6_out, and_7_out, and_8_out, and_10_out,
       and_11_out, and_12_out, not_1_out, not_2_out, not_3_out, not_4_out, not_5_out, not_6_out, not_7_out,
       not_8_out, not_9_out, not_10_out, not_11_out, not_12_out, not_13_out, not_14_out, not_15_out,
       not_16_out, not_17_out, not_18_out, not_19_out, not_20_out, not_21_out, or_1_out, or_2_out, or_3_out,
       or_4_out, or_5_out, t_ff_1_q, t_ff_2_q, t_ff_3_q, t_ff_4_q, xnor_1_out, xnor_2_out, xnor_3_out,
       xnor_4_out;

  and and_1 (and_1_out, 1'b1, not_1_out);
  and and_2 (and_2_out, t_ff_1_q, not_1_out);
  and and_3 (and_3_out, and_10_out, not_1_out);
  and and_4 (and_4_out, and_11_out, not_1_out);
  or or_1 (or_1_out, and_1_out, and_5_out);
  or or_2 (or_2_out, and_2_out, and_6_out);
  or or_3 (or_3_out, and_3_out, and_7_out);
  or or_4 (or_4_out, and_4_out, and_8_out);
  T_Flip_Flop t_ff_1 (.clk(in_1), .T(or_1_out), .Q(t_ff_1_q));  // open: Qn, preset, reset, en
  and and_5 (and_5_out, t_ff_1_q, or_5_out);
  T_Flip_Flop t_ff_2 (.clk(in_1), .T(or_2_out), .Q(t_ff_2_q));  // open: Qn, preset, reset, en
  and and_6 (and_6_out, t_ff_2_q, or_5_out);
  T_Flip_Flop t_ff_3 (.clk(in_1), .T(or_3_out), .Q(t_ff_3_q));  // open: Qn, preset, reset, en
  and and_7 (and_7_out, t_ff_3_q, or_5_out);
  T_Flip_Flop t_ff_4 (.clk(in_1), .T(or_4_out), .Q(t_ff_4_q));  // open: Qn, preset, reset, en
  and and_8 (and_8_out, t_ff_4_q, or_5_out);
  not not_1 (not_1_out, or_5_out);
  not not_2 (not_2_out, t_ff_1_q);
  not not_3 (not_3_out, t_ff_4_q);
  not not_4 (not_4_out, t_ff_3_q);
  not not_5 (not_5_out, t_ff_2_q);
  and and_9 (out_10, not_2_out, not_5_out, not_4_out, not_3_out);
  and and_10 (and_10_out, t_ff_1_q, t_ff_2_q);
  not not_6 (not_6_out, t_ff_4_q);
  not not_7 (not_7_out, t_ff_3_q);
  not not_8 (not_8_out, t_ff_2_q);
  and _1 (out_4, not_6_out, not_7_out, not_8_out, t_ff_1_q);
  and and_11 (and_11_out, and_10_out, t_ff_3_q);
  not not_9 (not_9_out, t_ff_4_q);
  not not_10 (not_10_out, t_ff_3_q);
  not not_11 (not_11_out, t_ff_1_q);
  not not_12 (not_12_out, t_ff_4_q);
  and _2 (out_5, not_9_out, not_10_out, t_ff_2_q, not_11_out);
  not not_13 (not_13_out, t_ff_3_q);
  not not_14 (not_14_out, t_ff_4_q);
  and _3 (out_6, not_12_out, not_13_out, t_ff_2_q, t_ff_1_q);
  or or_5 (or_5_out, and_12_out, in_3);
  not not_15 (not_15_out, t_ff_4_q);
  not not_16 (not_16_out, t_ff_2_q);
  not not_17 (not_17_out, t_ff_1_q);
  and _4 (out_11, not_14_out, t_ff_3_q, not_16_out, not_17_out);
  xnor xnor_1 (xnor_1_out, t_ff_1_q, in_2[0]);
  not not_18 (not_18_out, t_ff_2_q);
  not not_19 (not_19_out, t_ff_4_q);
  and _5 (out_7, not_15_out, t_ff_3_q, not_18_out, t_ff_1_q);
  xnor xnor_2 (xnor_2_out, t_ff_3_q, in_2[2]);
  xnor xnor_3 (xnor_3_out, t_ff_4_q, in_2[3]);
  xnor xnor_4 (xnor_4_out, t_ff_2_q, in_2[1]);
  and and_12 (and_12_out, xnor_3_out, xnor_2_out, xnor_4_out, xnor_1_out);
  not not_20 (not_20_out, t_ff_1_q);
  and _6 (out_8, not_19_out, t_ff_3_q, t_ff_2_q, not_20_out);
  not not_21 (not_21_out, t_ff_3_q);
  and _7 (out_9, t_ff_4_q, not_21_out, t_ff_2_q, t_ff_1_q);
endmodule
