// Logisim project CPU-Modified-PC.circ as structural Verilog: 12 circuits, main circuit trying_counter
module main (
  input  [3:0] in_1,
  input  in_2,
  input  in_3,
  input  [7:0] in_4,
  input  [7:0] in_5,
  input  in_6,
  input  in_7,
  output [7:0] out_8,
  output [7:0] out_9,
  output [7:0] out_10
);

  wire and_1_out, and_2_out, and_3_out, and_4_out, and_5_out, and_6_out, and_7_out, and_8_out, clock_1_out,
       clock_2_out, d_ff_1_q, main_1_out_11, main_2_out_2, main_2_out_3, main_2_out_4, main_2_out_5,
       main_2_out_6, main_2_out_7, main_2_out_8, main_3_out_2, main_3_out_3, main_3_out_4, main_3_out_5,
       main_3_out_6, main_3_out_7, main_3_out_8, main_4_out_2, main_4_out_3, main_4_out_4, main_4_out_5,
       main_4_out_6, main_4_out_7, main_4_out_8;
  wire [3:0] adder_1_out, multiplexer_1_out, register_1_q, yeah_1_out_21, yeah_1_out_22, yeah_1_out_23;
  wire [7:0] adder_2_out, mbr_1_out_5, RAM_out_5, register_2_q;

  _4BitCounter_main main_1 (
    .in_1(clock_1_out), .in_2(in_1), .in_3(in_2), .out_11(main_1_out_11));  // open: out_4, out_5, out_6, out_10, out_7, out_8, out_9
  Clock clock_1 (.out(clock_1_out));
  Multiplexer #(.width(4)) multiplexer_1 (
    .in0(4'b0000), .in1(4'b0001), .out(multiplexer_1_out), .sel(main_1_out_11));  // open: en
  Adder #(.width(4)) adder_1 (.a(multiplexer_1_out), .b(register_1_q), .out(adder_1_out));  // open: cin, cout
  MBR mbr_1 (.out_6(out_9), .in_1(in_5), .in_2(in_4), .in_3(in_6), .in_4(in_7), .out_5(mbr_1_out_5));
  Adder adder_2 (.a(register_2_q), .b(8'h7), .out(adder_2_out));  // open: cin, cout
  Register #(.width(4)) register_1 (.D(adder_1_out), .Q(register_1_q), .clk(clock_1_out));  // open: en, clr
  Register register_2 (.D(adder_2_out), .Q(register_2_q), .clk(clock_1_out));  // open: en, clr
  RAM RAM (.in_3(register_2_q), .in_1(in_3), .in_2(clock_1_out), .out_5(RAM_out_5), .in_4(register_1_q));
  _7_Segment_Display u_7_segment_display_1 (
    .g(main_2_out_2), .f(main_2_out_3), .a(main_2_out_4), .b(main_2_out_5), .e(main_2_out_8),
    .d(main_2_out_7), .c(main_2_out_6));  // open: dp
  Register register_3 (.D(RAM_out_5), .Q(out_8), .clk(clock_1_out));  // open: en, clr
  display_main main_2 (
    .in_1(yeah_1_out_23), .out_6(main_2_out_6), .out_7(main_2_out_7), .out_8(main_2_out_8),
    .out_2(main_2_out_2), .out_3(main_2_out_3), .out_4(main_2_out_4), .out_5(main_2_out_5));
  _7_Segment_Display u_7_segment_display_2 (
    .g(main_3_out_2), .f(main_3_out_3), .a(main_3_out_4), .b(main_3_out_5), .e(main_3_out_8),
    .d(main_3_out_7), .c(main_3_out_6));  // open: dp
  Yeah yeah_1 (
    .in_1(1'b0), .in_2(1'b0), .in_3(1'b0), .in_4(1'b0), .in_5(1'b0), .in_6(1'b0), .in_7(1'b0), .in_8(1'b0),
    .in_9(1'b0), .in_10(1'b0), .in_11(1'b0), .in_12(1'b0), .in_13(out_8[7]), .in_14(out_8[6]),
    .in_15(out_8[5]), .in_16(out_8[4]), .in_17(out_8[3]), .in_18(out_8[2]), .in_19(out_8[1]),
    .in_20(out_8[0]), .out_21(yeah_1_out_21), .out_22(yeah_1_out_22), .out_23(yeah_1_out_23));
  display_main main_3 (
    .in_1(yeah_1_out_22), .out_6(main_3_out_6), .out_7(main_3_out_7), .out_8(main_3_out_8),
    .out_2(main_3_out_2), .out_3(main_3_out_3), .out_4(main_3_out_4), .out_5(main_3_out_5));
  _7_Segment_Display u_7_segment_display_3 (
    .g(main_4_out_2), .f(main_4_out_3), .a(main_4_out_4), .b(main_4_out_5), .e(main_4_out_8),
    .d(main_4_out_7), .c(main_4_out_6));  // open: dp
  display_main main_4 (
    .in_1(yeah_1_out_21), .out_6(main_4_out_6), .out_7(main_4_out_7), .out_8(main_4_out_8),
    .out_2(main_4_out_2), .out_3(main_4_out_3), .out_4(main_4_out_4), .out_5(main_4_out_5));
  and and_1 (and_1_out, clock_2_out, clock_2_out);
  and and_2 (and_2_out, and_1_out, and_1_out);
  and and_3 (and_3_out, and_2_out, and_2_out);
  and and_4 (and_4_out, and_5_out, and_5_out);
  and and_5 (and_5_out, and_3_out, and_3_out);
  and and_6 (and_6_out, and_4_out, and_4_out);
  and and_7 (and_7_out, and_6_out, and_6_out);
  and and_8 (and_8_out, and_7_out, and_7_out);
  Clock clock_2 (.out(clock_2_out));
  D_Flip_Flop d_ff_1 (.clk(clock_2_out), .D(and_8_out), .Q(d_ff_1_q));  // open: Qn, preset, en, reset
endmodule

module ADD (
  input  [7:0] in_1,
  input  in_2,
  input  ITEM_5,
  input  ITEM_4,
  input  in_5,
  input  in_6,
  input  ITEM_2,
  input  in_8,
  input  in_9,
  input  in_10,
  output out_11
);

  wire and_1_out, and_2_out, and_3_out, and_4_out, clock_1_out, decoder_1_out0, decoder_1_out1,
       decoder_2_out0, decoder_2_out1;
  wire [7:0] adder_1_out_5, multiplexer_1_out, multiplexer_2_out, multiplexer_3_out, register_1_q,
       register_2_q, register_3_q, register_4_q, register_5_q;

  Multiplexer #(.width(8)) multiplexer_1 (
    .in0(in_1), .in1(register_5_q), .out(multiplexer_1_out), .sel(in_8));  // open: en
  Register register_1 (.D(multiplexer_1_out), .Q(register_1_q), .clk(and_1_out));  // open: en, clr
  and and_1 (and_1_out, decoder_1_out0, ITEM_5, clock_1_out);
  Decoder decoder_1 (.out0(decoder_1_out0), .out1(decoder_1_out1), .sel(ITEM_4));  // open: en
  Clock clock_1 (.out(clock_1_out));
  Register register_2 (.D(multiplexer_1_out), .Q(register_2_q), .clk(and_2_out));  // open: en, clr
  and and_2 (and_2_out, decoder_1_out1, ITEM_5, clock_1_out);
  Multiplexer #(.width(8)) multiplexer_2 (
    .in0(register_1_q), .in1(register_2_q), .out(multiplexer_2_out), .sel(in_5));  // open: en
  Multiplexer #(.width(8)) multiplexer_3 (
    .in0(multiplexer_1_out), .in1(multiplexer_2_out), .out(multiplexer_3_out), .sel(in_6));  // open: en
  Register register_3 (.D(multiplexer_3_out), .Q(register_3_q), .clk(and_3_out));  // open: en, clr
  and and_3 (and_3_out, clock_1_out, decoder_2_out0, decoder_2_out0);
  Decoder decoder_2 (.out0(decoder_2_out0), .out1(decoder_2_out1), .sel(ITEM_2));  // open: en
  Register register_4 (.D(multiplexer_3_out), .Q(register_4_q), .clk(and_4_out));  // open: en, clr
  and and_4 (and_4_out, clock_1_out, decoder_2_out1, decoder_2_out1);
  ADDER adder_1 (.in_1(in_2), .in_2(register_3_q), .in_3(register_4_q), .out_4(out_11), .out_5(adder_1_out_5));
  Register register_5 (.D(adder_1_out_5), .Q(register_5_q), .clk(clock_1_out));  // open: en, clr

  // Notes on the sheet:
  //   ITEM 1
  //   ITEM 3
  //   A-OUT
endmodule

module CONTROL_UNIT (
  input  [7:0] in_1,
  input  in_2,
  output out_3,
  output out_4,
  output out_5,
  output out_6,
  output out_7,
  output out_8,
  output out_9,
  output out_10,
  output out_11,
  output out_12,
  output out_13,
  output out_14,
  output out_15,
  output out_16,
  output out_17
);

  wire _00, _01, _10, _11, add, and_2_out, and_3_out, ARG1, ARG2, DEST, INP, not_1_out, not_2_out, not_3_out,
       not_4_out, not_5_out, not_6_out, not_7_out, not_8_out, not_9_out, not_10_out, not_11_out, not_12_out,
       not_13_out, not_14_out, not_15_out, not_16_out, not_17_out, or_2_out, or_3_out, or_4_out, or_5_out,
       PRT, STP, SUB;
  wire [3:0] _1TK, _3TX, _4TX, adder_1_out, jmp, multiplexer_6_out, multiplexer_7_out, or_6_out;
  wire [7:0] multiplexer_3_out, multiplexer_5_out;

  // AND_Gate and_1 is placed but not wired
  not not_1 (not_1_out, out_3);
  and and_2 (and_2_out, add, not_1_out);
  not not_2 (not_2_out, out_3);
  and and_3 (and_3_out, SUB, not_2_out);
  not not_3 (not_3_out, multiplexer_5_out[2]);
  not not_4 (not_4_out, multiplexer_5_out[1]);
  not not_5 (not_5_out, multiplexer_5_out[3]);
  not not_6 (not_6_out, multiplexer_5_out[1]);
  not not_7 (not_7_out, multiplexer_5_out[0]);
  not not_8 (not_8_out, multiplexer_5_out[2]);
  and u_ADD (add, multiplexer_5_out[3], not_3_out, not_6_out, not_7_out);
  and u_SUB (SUB, not_5_out, not_8_out, not_4_out, multiplexer_5_out[0]);
  or or_1 (out_16, and_2_out, and_3_out);
  not not_9 (not_9_out, multiplexer_5_out[3]);
  not not_10 (not_10_out, multiplexer_5_out[0]);
  not not_11 (not_11_out, multiplexer_5_out[3]);
  and u_PRT (PRT, not_11_out, not_9_out, multiplexer_5_out[1], not_10_out);
  or or_2 (or_2_out, SUB, add);
  or or_3 (or_3_out, PRT, INP);
  and and_4 (out_14, not_15_out, _01);
  not not_12 (not_12_out, multiplexer_5_out[3]);
  not not_13 (not_13_out, multiplexer_5_out[0]);
  not not_14 (not_14_out, multiplexer_5_out[3]);
  and u_STP (STP, not_14_out, multiplexer_5_out[2], multiplexer_5_out[1], not_13_out);
  Multiplexer #(.width(4)) multiplexer_1 (.in0(4'b0000), .in1(4'b0100), .out(_4TX), .sel(or_2_out));  // open: en
  Multiplexer #(.width(4)) multiplexer_2 (.in0(4'b0000), .in1(4'b0001), .out(_1TK), .sel(or_3_out));  // open: en
  not not_15 (not_15_out, multiplexer_3_out[0]);
  and and_5 (out_13, multiplexer_3_out[0], _01);
  not not_16 (not_16_out, multiplexer_5_out[0]);
  not not_17 (not_17_out, multiplexer_5_out[1]);
  and u_INP (INP, not_12_out, multiplexer_5_out[2], not_17_out, not_16_out);
  Multiplexer #(.width(8)) multiplexer_3 (
    .in0({8{1'b0}}), .in1(in_1), .out({multiplexer_3_out[7:6], DEST, multiplexer_3_out[4:0]}), .sel(_01));  // open: en
  or or_4 (or_4_out, add, SUB, _10, _11);
  and and_6 (out_15, or_4_out, out_7);
  Multiplexer #(.width(4)) multiplexer_4 (.in0(4'b0000), .in1(4'b0011), .out(_3TX), .sel(_01));  // open: en
  Multiplexer #(.width(8)) multiplexer_5 (
    .in0({8{1'b0}}), .in1(in_1), .out({multiplexer_5_out[7:6], ARG2, ARG1, multiplexer_5_out[3:0]}), .sel(_00));  // open: en
  or or_5 (or_5_out, add, SUB, _10, _11);
  and and_7 (out_17, or_5_out, out_8);
  assign or_6_out = _4TX | _1TK | jmp | _3TX;  // OR_Gate or_6, 4 bits wide
  // AND_Gate and_8 is placed but not wired
  Decoder #(.select(2)) decoder_1 (.out0(_00), .out1(_01), .out2(_10), .out3(_11), .sel(in_1[7:6]));  // open: en
  Adder #(.width(4)) adder_1 (.a(4'b0100), .b(or_6_out), .out(adder_1_out));  // open: cin, cout
  // _4BitCounter_main main_1: pin names not known; wires that end beside it: adder_1_out, STP
  assign jmp = multiplexer_6_out | multiplexer_7_out;  // OR_Gate or_7, 4 bits wide
  Multiplexer #(.width(4)) multiplexer_6 (
    .in0(4'b0000), .in1(4'b0101), .out(multiplexer_6_out), .sel(_10));  // open: en
  Multiplexer #(.width(4)) multiplexer_7 (
    .in0(4'b0000), .in1(4'b0101), .out(multiplexer_7_out), .sel(_11));  // open: en
  Multiplexer #(.width(8)) multiplexer_8 (.in0({8{1'b0}}), .in1(in_1), .sel(_10));  // open: out, en
  Multiplexer #(.width(8)) multiplexer_9 (.in0({8{1'b0}}), .in1(in_1), .sel(_11));  // open: out, en
  // AND_Gate and_9 is placed but not wired

  // Other names for the same wires on the sheet: _1 = out_4; _2 = out_5; _3 = out_6; _4 = out_7; _5 = out_8;
  //   _6 = out_9; _7 = out_10; _8 = out_11; _9 = out_12; BEQ = _10; BNQ = _11; CLK = in_2; INSTR[7:0] = in_1;
  //   LOAD = out_14; STORE = out_13; ZERO = out_3

  // Notes on the sheet:
  //   Writing to MAR
  //   Store in Register from A-Out (set mux to 1)
  //   ADDER PART
  //   Save to Left of ALU
  //   Save to Right of ALU
  //   Read mode of MBR
  //   MASTER_COUNTER
  //   Read/Write of RAM
endmodule

module trying_counter (
  input  in_1,
  input  in_2,
  input  ITEM_2,
  input  in_4,
  input  [7:0] in_5,
  input  [3:0] in_6,
  output out_7,
  output [7:0] out_8
);

  wire ADD, and_1_out, and_4_out, and_5_out, and_6_out, and_7_out, and_8_out, and_9_out, and_10_out,
       and_11_out, and_12_out, and_13_out, ARG1, ARG2, CLK, decoder_1_out0, decoder_1_out1, delay_1_out_2,
       delay_2_out_2, delay_3_out_2, EGT, FIVE, FOUR, LOAD, not_1_out, not_2_out, not_3_out, ONE, or_2_out,
       SIX, SVN, THREE, TWO;
  wire [3:0] adder_2_out, main_1_p1, mar_1_out_3, multiplexer_1_out, multiplexer_2_out, or_1_out,
       register_1_q, register_2_q;
  wire [7:0] adder_3_out_5, multiplexer_3_out, multiplexer_4_out, n8_bit_register_1_out_3,
       n8_bit_register_2_out_3, n8_bit_register_3_out_3, register_3_q, register_4_q, register_5_q;

  // _4BitCounter_main main_1: pin names not known; wires that end beside it: main_1_p1, in_1
  assign or_1_out = multiplexer_2_out | multiplexer_1_out;  // OR_Gate or_1, 4 bits wide
  Multiplexer #(.width(4)) multiplexer_1 (
    .in0(4'b0000), .in1(4'b0100), .out(multiplexer_1_out), .sel(and_1_out));  // open: en
  Adder #(.width(4)) adder_1 (.a(4'b0100), .b(register_2_q), .out(main_1_p1));  // open: cin, cout
  Adder #(.width(4)) adder_2 (.a(4'b0001), .b(register_1_q), .out(adder_2_out));  // open: cin, cout
  RAM ram_1 (.in_3(in_5), .in_1(in_4), .in_2(CLK), .out_5(out_8), .in_4(mar_1_out_3));
  not not_1 (not_1_out, register_3_q[6]);
  not not_2 (not_2_out, register_3_q[7]);
  and and_1 (and_1_out, not_2_out, not_1_out);
  // AND_Gate and_2 has open pins: in1=and_1_out, out=open
  Register #(.width(4)) register_1 (.D(adder_2_out), .Q(register_1_q), .clk(delay_1_out_2));  // open: en, clr
  DELAY delay_1 (.in_1(TWO), .out_2(delay_1_out_2));
  Register #(.width(4)) register_2 (.D(or_1_out), .Q(register_2_q), .clk(FOUR));  // open: en, clr
  and and_3 (LOAD, register_3_q[7], not_3_out);
  Multiplexer #(.width(4)) multiplexer_2 (
    .in0(4'b0000), .in1(4'b0100), .out(multiplexer_2_out), .sel(LOAD));  // open: en
  MAR mar_1 (.in_1(register_1_q), .in_2(ONE), .out_3(mar_1_out_3));
  not not_3 (not_3_out, register_3_q[6]);
  Register register_3 (
    .D(out_8), .Q({register_3_q[7:6], ARG1, ARG2, register_3_q[3:0]}), .clk(THREE));  // open: en, clr
  and and_4 (and_4_out, EGT, CLK);
  _8_bit_register u_8_bit_register_1 (.in_1(register_5_q), .in_2(and_5_out), .out_3(n8_bit_register_1_out_3));
  and and_5 (and_5_out, decoder_1_out0, and_4_out, CLK);
  Decoder decoder_1 (.out0(decoder_1_out0), .out1(decoder_1_out1), .sel(and_6_out));  // open: en
  Clock clock_1 (.out(CLK));
  and and_6 (and_6_out, ARG1, ADD);
  Register register_4 (.D(register_5_q), .Q(register_4_q), .clk(and_7_out));  // open: en, clr
  and and_7 (and_7_out, decoder_1_out1, and_4_out, CLK);
  and and_8 (and_8_out, FIVE, ARG1);
  Multiplexer #(.width(8)) multiplexer_3 (
    .in0(n8_bit_register_1_out_3), .in1(register_4_q), .out(multiplexer_3_out), .sel(or_2_out));  // open: en
  or or_2 (or_2_out, and_8_out, and_10_out, and_9_out);
  and and_9 (and_9_out, SIX, ARG2);
  Multiplexer #(.width(8)) multiplexer_4 (
    .in0(register_5_q), .in1(multiplexer_3_out), .out(multiplexer_4_out), .sel(1'b1));  // open: en
  and and_10 (and_10_out, FOUR, ARG1);
  _8_bit_register u_8_bit_register_2 (.in_1(multiplexer_4_out), .in_2(and_11_out), .out_3(n8_bit_register_2_out_3));
  and and_11 (and_11_out, delay_2_out_2, FIVE);
  DELAY delay_2 (.in_1(CLK), .out_2(delay_2_out_2));
  and and_12 (and_12_out, delay_3_out_2, SIX);
  DELAY delay_3 (.in_1(CLK), .out_2(delay_3_out_2));
  ADDER adder_3 (
    .in_1(in_2), .in_2(n8_bit_register_2_out_3), .in_3(n8_bit_register_3_out_3), .out_4(out_7),
    .out_5(adder_3_out_5));
  _8_bit_register u_8_bit_register_3 (.in_1(multiplexer_4_out), .in_2(and_12_out), .out_3(n8_bit_register_3_out_3));
  Register register_5 (.D(adder_3_out_5), .Q(register_5_q), .clk(and_13_out));  // open: en, clr
  and and_13 (and_13_out, CLK, SVN);
  T_Flip_Flop t_ff_1 (.clk(and_13_out), .T(1'b1));  // open: Q, Qn, preset, reset, en
  // NOT_Gate not_4 is placed but not wired

  // Notes on the sheet:
  //   NOTE: ADD AND GATE IN TIMER
  //   IDEA: SEPARATE RAM INTO DATA AND INSTRUCTION FIELDS
  //   ITEM 4
  //   ITEM 1
  //   ITEM 3
  //   A-OUT
endmodule

module DELAY (
  input  in_1,
  output out_2
);

  wire and_1_out, and_2_out, and_3_out, and_4_out, and_5_out, and_6_out, and_7_out, and_8_out, and_9_out,
       and_10_out, and_11_out, and_12_out, and_13_out, and_14_out, and_15_out;

  and and_1 (and_1_out, in_1, in_1);
  and and_2 (and_2_out, and_3_out, and_3_out);
  and and_3 (and_3_out, and_1_out, and_1_out);
  and and_4 (and_4_out, and_2_out, and_2_out);
  and and_5 (and_5_out, and_4_out, and_4_out);
  and and_6 (and_6_out, and_5_out, and_5_out);
  and and_7 (and_7_out, and_6_out, and_6_out);
  and and_8 (and_8_out, and_7_out, and_7_out);
  and and_9 (and_9_out, and_8_out, and_8_out);
  and and_10 (and_10_out, and_9_out, and_9_out);
  and and_11 (and_11_out, and_10_out, and_10_out);
  and and_12 (and_12_out, and_11_out, and_11_out);
  and and_13 (and_13_out, and_12_out, and_12_out);
  and and_14 (and_14_out, and_13_out, and_13_out);
  and and_15 (and_15_out, and_14_out, and_14_out);
  and and_16 (out_2, and_15_out, and_15_out);
endmodule

module _8_bit_register (
  input  [7:0] in_1,
  input  in_2,
  output [7:0] out_3
);

  D_Flip_Flop d_ff_1 (.clk(in_2), .D(in_1[7]), .Q(out_3[7]));  // open: Qn, preset, en, reset
  D_Flip_Flop d_ff_2 (.clk(in_2), .D(in_1[6]), .Q(out_3[6]));  // open: Qn, preset, en, reset
  D_Flip_Flop d_ff_3 (.clk(in_2), .D(in_1[5]), .Q(out_3[5]));  // open: Qn, preset, en, reset
  D_Flip_Flop d_ff_4 (.clk(in_2), .D(in_1[4]), .Q(out_3[4]));  // open: Qn, preset, en, reset
  D_Flip_Flop d_ff_5 (.clk(in_2), .D(in_1[3]), .Q(out_3[3]));  // open: Qn, preset, en, reset
  D_Flip_Flop d_ff_6 (.clk(in_2), .D(in_1[2]), .Q(out_3[2]));  // open: Qn, preset, en, reset
  D_Flip_Flop d_ff_7 (.clk(in_2), .D(in_1[1]), .Q(out_3[1]));  // open: Qn, preset, en, reset
  D_Flip_Flop d_ff_8 (.clk(in_2), .D(in_1[0]), .Q(out_3[0]));  // open: Qn, preset, en, reset
endmodule

module BOARD (
  input  [7:0] in_1,
  input  in_2,
  input  in_3,
  input  RAM_mode,
  input  in_5,
  input  in_6,
  input  in_7,
  input  in_8,
  input  in_9,
  input  in_10,
  input  ITEM_2,
  output out_12
);

  wire and_1_out, and_2_out, and_3_out, CLK, control_unit_1_out_3, control_unit_1_out_4,
       control_unit_1_out_5, control_unit_1_out_6, control_unit_1_out_7, control_unit_1_out_8,
       control_unit_1_out_9, control_unit_1_out_10, control_unit_1_out_11, control_unit_1_out_13,
       delay_1_out_2, delay_2_out_2, delay_3_out_2, FIVE, SIX, SVN, undriven, undriven_2, undriven_3,
       undriven_4;
  wire [3:0] adder_1_out, MAR_q, multiplexer_4_out, multiplexer_5_out, n8to4_1_out_2, PC_q;
  wire [7:0] adder_2_out_5, IR_q, MBR_out_5, MBR_out_6, multiplexer_1_out, multiplexer_2_out,
       multiplexer_3_out, multiplexer_6_out, multiplexer_7_out, n8_bit_register_1_out_3,
       n8_bit_register_2_out_3, n8_bit_register_3_out_3, ram_1_out_5, register_1_q, register_2_q;

  RAM ram_1 (.in_3(multiplexer_1_out), .in_1(RAM_mode), .in_2(CLK), .out_5(ram_1_out_5), .in_4(multiplexer_5_out));
  Multiplexer #(.width(8)) multiplexer_1 (
    .in0(in_1), .in1(MBR_out_5), .out(multiplexer_1_out), .sel(in_3));  // open: en
  Multiplexer #(.width(8)) multiplexer_2 (
    .in0(ram_1_out_5), .in1(multiplexer_1_out), .out(multiplexer_2_out), .sel(in_7));  // open: en
  Clock clock_1 (.out(CLK));
  Multiplexer #(.width(8)) multiplexer_3 (
    .in0(register_2_q), .in1(MBR_out_6), .out(multiplexer_3_out), .sel(in_9));  // open: en
  MBR MBR (
    .out_6(MBR_out_6), .in_1(multiplexer_7_out), .in_2(multiplexer_2_out), .in_3(in_8), .in_4(CLK),
    .out_5(MBR_out_5));
  _8to4 u_8to4_1 (.in_1(multiplexer_3_out), .out_2(n8to4_1_out_2));
  Multiplexer #(.width(4)) multiplexer_4 (
    .in0(PC_q), .in1(n8to4_1_out_2), .out(multiplexer_4_out), .sel(in_6));  // open: en
  Multiplexer #(.width(4)) multiplexer_5 (.in1(MAR_q), .out(multiplexer_5_out), .sel(in_5));  // open: in0, en
  Register #(.width(4)) MAR (.D(multiplexer_4_out), .Q(MAR_q));  // open: en, clk, clr
  _8_bit_register u_8_bit_register_1 (.in_1(multiplexer_3_out), .in_2(undriven), .out_3(n8_bit_register_1_out_3));
  Register register_1 (.D(multiplexer_3_out), .Q(register_1_q), .clk(undriven_2));  // open: en, clr
  Multiplexer #(.width(8)) multiplexer_6 (
    .in0(n8_bit_register_1_out_3), .in1(register_1_q), .out(multiplexer_6_out), .sel(undriven_3));  // open: en
  Register #(.width(4)) PC (.D(adder_1_out), .Q(PC_q), .clk(delay_1_out_2));  // open: en, clr
  Adder #(.width(4)) adder_1 (.a(4'b0001), .b(PC_q), .out(adder_1_out));  // open: cin, cout
  DELAY delay_1 (.in_1(in_2), .out_2(delay_1_out_2));
  Multiplexer #(.width(8)) multiplexer_7 (
    .in0(multiplexer_6_out), .in1(multiplexer_3_out), .out(multiplexer_7_out));  // open: sel, en
  and and_1 (and_1_out, delay_2_out_2, FIVE);
  DELAY delay_2 (.in_1(undriven_4), .out_2(delay_2_out_2));
  _8_bit_register u_8_bit_register_2 (.in_1(multiplexer_7_out), .in_2(and_1_out), .out_3(n8_bit_register_2_out_3));
  and and_2 (and_2_out, delay_3_out_2, SIX);
  DELAY delay_3 (.in_1(undriven_4), .out_2(delay_3_out_2));
  ADDER adder_2 (
    .in_1(in_10), .in_2(n8_bit_register_2_out_3), .in_3(n8_bit_register_3_out_3), .out_4(out_12),
    .out_5(adder_2_out_5));
  _8_bit_register u_8_bit_register_3 (.in_1(multiplexer_7_out), .in_2(and_2_out), .out_3(n8_bit_register_3_out_3));
  Register register_2 (.D(adder_2_out_5), .Q(register_2_q), .clk(and_3_out));  // open: en, clr
  buf and_3 (and_3_out, SVN);  // AND_Gate
  Register IR (.D(MBR_out_5), .Q(IR_q));  // open: en, clk, clr
  CONTROL_UNIT control_unit_1 (
    .in_2(CLK), .in_1(IR_q), .out_13(control_unit_1_out_13), .out_3(control_unit_1_out_3),
    .out_4(control_unit_1_out_4), .out_5(control_unit_1_out_5), .out_6(control_unit_1_out_6),
    .out_7(control_unit_1_out_7), .out_8(control_unit_1_out_8), .out_9(control_unit_1_out_9),
    .out_10(control_unit_1_out_10), .out_11(control_unit_1_out_11));  // open: out_16, out_15, out_17, out_14, out_12
  // NOT_Gate not_1 is placed but not wired

  // Other names for the same wires on the sheet: TWO = in_2

  // Notes on the sheet:
  //   When storing from MAR to AR, make long delay
  //   Toggled when reading to RAM
  //   SYSTEM BUS
  //   CPU BUS
  //   GP Registers
  //   Toggled when AR <- MAR
  //   ITEM 4
  //   ITEM 1
  //   A-OUT
endmodule

module MBR (
  input  [7:0] in_1,
  input  [7:0] in_2,
  input  in_3,
  input  in_4,
  output [7:0] out_5,
  output [7:0] out_6
);

  wire [7:0] d_ff_8_q, multiplexer_1_out;

  Multiplexer #(.width(8)) multiplexer_1 (.in0(in_1), .in1(in_2), .out(multiplexer_1_out), .sel(in_3));  // open: en
  D_Flip_Flop d_ff_1 (.clk(in_4), .D(multiplexer_1_out[7]), .Q(d_ff_8_q[7]));  // open: Qn, preset, en, reset
  D_Flip_Flop d_ff_2 (.clk(in_4), .D(multiplexer_1_out[6]), .Q(d_ff_8_q[6]));  // open: Qn, preset, en, reset
  D_Flip_Flop d_ff_3 (.clk(in_4), .D(multiplexer_1_out[5]), .Q(d_ff_8_q[5]));  // open: Qn, preset, en, reset
  D_Flip_Flop d_ff_4 (.clk(in_4), .D(multiplexer_1_out[4]), .Q(d_ff_8_q[4]));  // open: Qn, preset, en, reset
  D_Flip_Flop d_ff_5 (.clk(in_4), .D(multiplexer_1_out[3]), .Q(d_ff_8_q[3]));  // open: Qn, preset, en, reset
  D_Flip_Flop d_ff_6 (.clk(in_4), .D(multiplexer_1_out[2]), .Q(d_ff_8_q[2]));  // open: Qn, preset, en, reset
  Demultiplexer #(.width(8)) demultiplexer_1 (.out0(out_5), .out1(out_6), .in(d_ff_8_q), .sel(in_3));  // open: en
  D_Flip_Flop d_ff_7 (.clk(in_4), .D(multiplexer_1_out[1]), .Q(d_ff_8_q[1]));  // open: Qn, preset, en, reset
  D_Flip_Flop d_ff_8 (.clk(in_4), .D(multiplexer_1_out[0]), .Q(d_ff_8_q[0]));  // open: Qn, preset, en, reset
endmodule

module MAR (
  input  [3:0] in_1,
  input  in_2,
  output [3:0] out_3
);

  D_Flip_Flop d_ff_1 (.clk(in_2), .D(in_1[3]), .Q(out_3[3]));  // open: Qn, preset, en, reset
  D_Flip_Flop d_ff_2 (.clk(in_2), .D(in_1[2]), .Q(out_3[2]));  // open: Qn, preset, en, reset
  D_Flip_Flop d_ff_3 (.clk(in_2), .D(in_1[1]), .Q(out_3[1]));  // open: Qn, preset, en, reset
  D_Flip_Flop d_ff_4 (.clk(in_2), .D(in_1[0]), .Q(out_3[0]));  // open: Qn, preset, en, reset
endmodule

module _8to4 (
  input  [7:0] in_1,
  output [3:0] out_2
);


  assign out_2 = in_1[3:0];
endmodule

module _4to8 (
  input  [3:0] in_1,
  output [7:0] out_2
);


  assign out_2 = {4'b0000, in_1};
endmodule

module PC (
  input  [3:0] in_1,
  input  in_2,
  output [3:0] out_3
);

  D_Flip_Flop d_ff_1 (.clk(in_2), .D(in_1[3]), .Q(out_3[3]));  // open: Qn, preset, en, reset
  D_Flip_Flop d_ff_2 (.clk(in_2), .D(in_1[2]), .Q(out_3[2]));  // open: Qn, preset, en, reset
  D_Flip_Flop d_ff_3 (.clk(in_2), .D(in_1[1]), .Q(out_3[1]));  // open: Qn, preset, en, reset
  D_Flip_Flop d_ff_4 (.clk(in_2), .D(in_1[0]), .Q(out_3[0]));  // open: Qn, preset, en, reset
endmodule
